# Fritzing sketch vs1053b Sketch 1 (saved by Fritzing 0.9.3b)
stripboards: 1

parts:
  IC1 = IC, DIP package, 8 pins [chip_label=6N139]
  R1 = Resistor [tolerance=±5% resistance=220 package=THT]
  R2 = Resistor [tolerance=±5% resistance=10k package=THT]
  R3 = Resistor [tolerance=±5% resistance=220 package=THT]
  R4 = Resistor [tolerance=±5% resistance=10k package=THT]
  R5 = Resistor [tolerance=±5% resistance=10k package=THT]
  R6 = Resistor [tolerance=±5% resistance=10k package=THT]
  R7 = Resistor [tolerance=±5% resistance=10k package=THT]
  R8 = Resistor [tolerance=±5% resistance=10k package=THT]
  R9 = Resistor [tolerance=±5% resistance=10k package=THT]
  C1 = Ceramic Capacitor [capacitance=100nF package="100 mil [THT, multilayer]"]
  C2 = Ceramic Capacitor [capacitance=100nF package="100 mil [THT, multilayer]"]
  Y1 = CRYSTAL [part_number="16 MHz" package=hc49u-v]
  R10 = Resistor [tolerance=±5% resistance=470k package=THT]
  U4 = MIDI_CONN_FEMALE [package=din_5_female]
  U1 = atmega328 [package=dip]
  S1 = Pushbutton [package="[THT]"]
  S2 = Pushbutton [package="[THT]"]
  S3 = Pushbutton [package="[THT]"]
  WeMos_D1_Mini_OLED_Shield1 = WeMos D1 Mini OLED Shield
  Part1 = Adafruit VS1053 Codec + MicroSD Breakout - MP3/WAV/MIDI/OGG [part_number="Adafruit #1381"]
  JACK1 = 2.1mm DC Barrel Jack
  TRS1 = Audio Jack (TRS) 3.5mm [package="4Ucon 08780 [THT]"]
  C3 = Capacitor Polarized [package=cpol-radial-10uf-25v]
  C4 = Capacitor [package=cap-pth-large]
  R11 = Resistor [tolerance=±5% resistance=470k package=THT]
  LED1 = LED - 5mm [color="Red (633nm)" package="5 mm [THT]"]

nets:
  N1: IC1.pin2, R1.Pin_0
  N2: IC1.pin3, U4.MIDI_IN
  GND: IC1.pin5, R2.Pin_1, R7.Pin_1, R8.Pin_0, R9.Pin_0, C1.1, C2.1, U1.GND, WeMos_D1_Mini_OLED_Shield1.G, Part1.GND, C3.-, C4.1, LED1.cathode
  N3: IC1.pin6, U1.D0_(RX), R11.Pin_0
  N4: IC1.pin7, R2.Pin_0
  VCC: IC1.pin8, R4.Pin_1, R5.Pin_1, R6.Pin_1, U1.VCC, U1.AVCC, U1.AREF, S1.Pin_1, S2.Pin_1, S2.Pin_2, S3.Pin_3, S3.Pin_4, Part1.VIN, JACK1.center, JACK1.sleeve, C3.+, C4.2, R11.Pin_1
  N5: R1.Pin_1, U4.MIDI_OUT
  N6: R3.Pin_0, Part1.RX_5V
  N7: R3.Pin_1, U1.D1_(TX)
  N8: R4.Pin_0, U1.RESET
  N9: R5.Pin_0, U1.A5, WeMos_D1_Mini_OLED_Shield1.D1
  N10: R6.Pin_0, U1.A4, WeMos_D1_Mini_OLED_Shield1.D2
  N11: R7.Pin_0, U1.D5_(PWM), S3.Pin_1
  N12: R8.Pin_1, U1.D7, S1.Pin_3
  N13: R9.Pin_1, U1.D6_(PWM), S2.Pin_3
  N14: C1.0, Y1.1, U1.XLAT1
  N15: C2.0, Y1.2, U1.XLAT2
  N16: R10.Pin_0, LED1.anode
  N17: R10.Pin_1, U1.D2
  N18: U1.D3_(PWM), Part1.DREQ
  N19: U1.D4, Part1.SDCS_5V
  N20: U1.D8, Part1.XDCS_5V
  N21: U1.D9_(PWM), Part1.RST_5V
  N22: U1.D10_(PWM), Part1.CS_5V
  N23: U1.D11_(PWM), Part1.MOSI_5V
  N24: U1.D12, Part1.MISO
  N25: U1.D13, Part1.SCLK_5V
  3V3: WeMos_D1_Mini_OLED_Shield1.3V3, Part1.3.3V
  N26: Part1.R_OUT, TRS1.Ring
  N27: Part1.L_OUT, TRS1.Tip
  N28: Part1.AGND, TRS1.Sleeve

custom parts:
  Adafruit VS1053 Codec + MicroSD Breakout - MP3/WAV/MIDI/OGG: This breakout board is the ultimate companion for the VLSI VS1053B DSP codec chip. The VS1053 can decode a wide variety of audio formats such as MP3, AAC, Ogg Vorbis, WMA, MIDI, FLAC, WAV (PCM and ADPCM). It can also be used to record audio in both PCM (WAV) and compressed Ogg Vorbis. You can do all sorts of stuff with the audio as well such as adjusting bass, treble, and volume digitally.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
  2.1mm DC Barrel Jack: 2.1mm DC Barrel Jack with Thru-Hole Connectors (breadboardable)
